# Fritzing sketch Lab-01-07 (saved by Fritzing 0.9.2b)
breadboards: 1

parts:
  PART1 = Pi Wedge B+
  LED1 = LED - 5mm [color="Red (633nm)" package="5 mm [THT]"]
  R1 = Resistor [tolerance=±5% resistance=330 package=THT]

nets:
  N1: PART1.GPIO_4_(GPCLK0), PART1.G4, LED1.cathode
  N2: PART1.3.3V#72, R1.Pin_1
  N3: LED1.anode, R1.Pin_0

custom parts:
  Pi Wedge B+: This is the Pi Wedge B Plus, a board that connects to the Raspberry Pi B+’s 40-pin GPIO connector, and breaks the pins out to breadboard-friendly arrangement and spacing, and even adds a couple of decoupling capacitors on the power supply lines. The “Wedge” also makes the initial bringup process easier - you can plug an FTDI Basic module into the built-in serial port. Each Pi Wedge comes as an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
