# Fritzing sketch Lab-03-05 (saved by Fritzing 0.9.2b)
breadboards: 1

parts:
  PART1 = Pi Wedge B+
  LED1 = LED - 5mm [color="Red (633nm)" package="5 mm [THT]"]
  R1 = Resistor [tolerance=±5% resistance=330 package=THT]
  LED2 = smd LED [color="Yellow (585nm)" package="1206 [SMD]"]
  R2 = Resistor [tolerance=±5% resistance=330 package=THT]
  S1 = Pushbutton [package="[SMD]"]

nets:
  N1: PART1.GPIO_5, PART1.G5, LED2.cathode
  N2: PART1.G6, S1.Pin_1, S1.Pin_2
  N3: PART1.G4, LED1.cathode
  N4: PART1.GND, S1.Pin_3, S1.Pin_4
  N5: PART1.3.3V#72, R1.Pin_1, R2.Pin_1
  N6: LED1.anode, R1.Pin_0
  N7: LED2.anode, R2.Pin_0

custom parts:
  Pi Wedge B+: This is the Pi Wedge B Plus, a board that connects to the Raspberry Pi B+’s 40-pin GPIO connector, and breaks the pins out to breadboard-friendly arrangement and spacing, and even adds a couple of decoupling capacitors on the power supply lines. The “Wedge” also makes the initial bringup process easier - you can plug an FTDI Basic module into the built-in serial port. Each Pi Wedge comes as an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
