# Fritzing sketch Lab-04-04 (saved by Fritzing 0.9.2b)
breadboards: 1

parts:
  PART1 = Pi Wedge B+
  U1 = IC, DIP package, 16 pins [chip_label=MCP3008]

nets:
  N1: PART1.3.3V#19, PART1.3.3V#55, U1.pin15, U1.pin16

custom parts:
  Pi Wedge B+: This is the Pi Wedge B Plus, a board that connects to the Raspberry Pi B+’s 40-pin GPIO connector, and breaks the pins out to breadboard-friendly arrangement and spacing, and even adds a couple of decoupling capacitors on the power supply lines. The “Wedge” also makes the initial bringup process easier - you can plug an FTDI Basic module into the built-in serial port. Each Pi Wedge comes as an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
