# Fritzing sketch Lab-04-12 (saved by Fritzing 0.9.2b)
breadboards: 1

parts:
  PART1 = Pi Wedge B+
  U1 = IC, DIP package, 16 pins [chip_label=MCP3008]
  T1 = TMP36 Temperature Sensor [package="TO92 [THT]"]
  C2 = Capacitor [package=cap-pth-small]

nets:
  N1: PART1.3.3V#19, PART1.3.3V#55, U1.pin15, U1.pin16
  N2: PART1.CE0, U1.pin10
  N3: PART1.MOSI, U1.pin11
  N4: PART1.MISO, U1.pin12
  N5: PART1.SCK, U1.pin13
  N6: PART1.GND, U1.pin9, U1.pin14
  N7: T1.Vout, C2.2
  N8: T1.GND, C2.1

custom parts:
  Pi Wedge B+: This is the Pi Wedge B Plus, a board that connects to the Raspberry Pi B+’s 40-pin GPIO connector, and breaks the pins out to breadboard-friendly arrangement and spacing, and even adds a couple of decoupling capacitors on the power supply lines. The “Wedge” also makes the initial bringup process easier - you can plug an FTDI Basic module into the built-in serial port. Each Pi Wedge comes as an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
